# Fritzing sketch Sensor de linea (saved by Fritzing 0.9.2b)
breadboards: 1

parts:
  R1 = Resistor [tolerance=±5% resistance=220 package=THT]  # not connected
  Op1 = LMV324 [package=so014]
  R2 = TRIMPOT [package=trim_pot_pth]  # not connected
  Op2 = LMV324 [package=so014]
  J1 = male pin header, 10 pins [form="♂ (male)"]

nets:
  p1: Op1.G$1_OUT, J1.pin1
  5V: Op1.G$1_+V, Op2.G$1_+V, J1.pin9
  p2: Op1.G$2_OUT, J1.pin2
  p3: Op1.G$3_OUT, J1.pin3
  GND: Op1.G$1_-V, Op2.G$1_-V, J1.pin10
  p4: Op1.G$4_OUT, J1.pin4
  p5: Op2.G$1_OUT, J1.pin5
  p6: Op2.G$2_OUT, J1.pin6
  p7: Op2.G$3_OUT, J1.pin7
  p8: Op2.G$4_OUT, J1.pin8
